// Logisim project mikro.circ as structural Verilog: 10 circuits, main circuit main
module main (
);

  wire clock_1_out, undriven_3;
  wire [3:0] undriven_4, undriven_5, undriven_6, undriven_7;
  wire [11:0] undriven;
  wire [15:0] ram_1_data, undriven_2;

  Hex_Digit_Display hex_digit_display_1 (.value(undriven_7));  // open: dp
  Hex_Digit_Display hex_digit_display_2 (.value(undriven_6));  // open: dp
  Hex_Digit_Display hex_digit_display_3 (.value(undriven_5));  // open: dp
  CPU CPU (
    .D_IN(ram_1_data), .D_OUT(undriven_2), .ADDR(undriven),
    .Register_0({undriven_7, undriven_6, undriven_5, undriven_4}));
  Hex_Digit_Display hex_digit_display_4 (.value(undriven_4));  // open: dp
  Clock clock_1 (.out(clock_1_out));
  RAM #(.addrWidth(12), .dataWidth(16), .bus("separate")) ram_1 (
    .addr(undriven), .din(undriven_2), .data(ram_1_data), .str(undriven_3), .clk(clock_1_out));  // open: sel, ld, clr
endmodule

module ALU (
  input  [15:0] A,
  input  [15:0] B,
  input  [2:0] IR_11_9,
  input  [2:0] IR_8_6,
  output [15:0] R3,
  output ZF
);

  wire [15:0] _16_bit_AND_out, _16_bit_OR_out, _16_bit_XOR_out, adder_1_out, adder_2_out, multiplexer_1_out,
       not_1_out, subtractor_1_out, subtractor_2_out;

  Adder #(.width(16)) adder_1 (.a(A), .b(B), .out(adder_1_out));  // open: cin, cout
  Subtractor #(.width(16)) subtractor_1 (.a(A), .b(B), .out(subtractor_1_out));  // open: bin, bout
  assign _16_bit_AND_out = A & B;  // AND_Gate _16_bit_AND, 16 bits wide
  assign _16_bit_OR_out = A | B;  // OR_Gate _16_bit_OR, 16 bits wide
  assign _16_bit_XOR_out = A ^ B;  // XOR_Gate _16_bit_XOR, 16 bits wide
  assign not_1_out = ~A;  // NOT_Gate not_1, 16 bits wide
  Adder #(.width(16)) adder_2 (.a(A), .b(16'h1), .out(adder_2_out));  // open: cin, cout
  Subtractor #(.width(16)) subtractor_2 (.a(A), .b(16'h1), .out(subtractor_2_out));  // open: bin, bout
  Multiplexer #(.select(3), .width(16), .enable("false")) multiplexer_1 (
    .in0(not_1_out), .in1(A), .in2(adder_2_out), .in3(subtractor_2_out), .out(multiplexer_1_out), .sel(IR_8_6));  // open: in4, in5, in6, in7
  Multiplexer #(.select(3), .width(16), .enable("false")) multiplexer_2 (
    .in0(adder_1_out), .in1(subtractor_1_out), .in2(_16_bit_AND_out), .in3(_16_bit_OR_out),
    .in4(_16_bit_XOR_out), .in7(multiplexer_1_out), .out(R3), .sel(IR_11_9));  // open: in5, in6
  nor nor_1 (ZF, R3[15], R3[14], R3[13], R3[12], R3[11], R3[10], R3[9], R3[8], R3[7], R3[6], R3[5], R3[4], R3[3], R3[2], R3[1], R3[0]);
endmodule

module _16_bit_register (
  input  [15:0] Input_16_Bits,
  input  in_2,
  output [15:0] Output_16_Bits
);

  wire and_1_out, and_2_out, and_3_out, and_4_out, and_5_out, and_6_out, and_7_out, and_8_out, and_9_out,
       and_10_out, and_11_out, and_12_out, and_13_out, and_14_out, and_15_out, and_16_out, and_17_out,
       and_18_out, and_19_out, and_20_out, and_21_out, and_22_out, and_23_out, and_24_out, and_25_out,
       and_26_out, and_27_out, and_28_out, and_29_out, and_30_out, and_31_out, and_32_out, clock_1_out,
       not_1_out, not_2_out, not_3_out, not_4_out, not_5_out, not_6_out, not_7_out, not_8_out, not_9_out,
       not_10_out, not_11_out, not_12_out, not_13_out, not_14_out, not_15_out, not_16_out;

  not not_1 (not_1_out, Input_16_Bits[0]);
  and and_1 (and_1_out, not_1_out, in_2);
  not not_2 (not_2_out, Input_16_Bits[1]);
  and and_2 (and_2_out, not_2_out, in_2);
  not not_3 (not_3_out, Input_16_Bits[2]);
  and and_3 (and_3_out, not_3_out, in_2);
  not not_4 (not_4_out, Input_16_Bits[3]);
  and and_4 (and_4_out, not_4_out, in_2);
  not not_5 (not_5_out, Input_16_Bits[4]);
  and and_5 (and_5_out, not_5_out, in_2);
  not not_6 (not_6_out, Input_16_Bits[5]);
  and and_6 (and_6_out, not_6_out, in_2);
  not not_7 (not_7_out, Input_16_Bits[6]);
  and and_7 (and_7_out, not_7_out, in_2);
  not not_8 (not_8_out, Input_16_Bits[7]);
  and and_8 (and_8_out, not_8_out, in_2);
  not not_9 (not_9_out, Input_16_Bits[8]);
  and and_9 (and_9_out, not_9_out, in_2);
  not not_10 (not_10_out, Input_16_Bits[9]);
  and and_10 (and_10_out, not_10_out, in_2);
  not not_11 (not_11_out, Input_16_Bits[10]);
  and and_11 (and_11_out, not_11_out, in_2);
  not not_12 (not_12_out, Input_16_Bits[11]);
  and and_12 (and_12_out, not_12_out, in_2);
  not not_13 (not_13_out, Input_16_Bits[12]);
  and and_13 (and_13_out, not_13_out, in_2);
  not not_14 (not_14_out, Input_16_Bits[13]);
  and and_14 (and_14_out, not_14_out, in_2);
  not not_15 (not_15_out, Input_16_Bits[14]);
  and and_15 (and_15_out, not_15_out, in_2);
  not not_16 (not_16_out, Input_16_Bits[15]);
  and and_16 (and_16_out, not_16_out, in_2);
  and and_17 (and_17_out, Input_16_Bits[0], in_2);
  and and_18 (and_18_out, Input_16_Bits[1], in_2);
  and and_19 (and_19_out, Input_16_Bits[2], in_2);
  and and_20 (and_20_out, Input_16_Bits[3], in_2);
  and and_21 (and_21_out, Input_16_Bits[4], in_2);
  and and_22 (and_22_out, Input_16_Bits[5], in_2);
  and and_23 (and_23_out, Input_16_Bits[6], in_2);
  and and_24 (and_24_out, Input_16_Bits[7], in_2);
  and and_25 (and_25_out, Input_16_Bits[8], in_2);
  and and_26 (and_26_out, Input_16_Bits[9], in_2);
  and and_27 (and_27_out, Input_16_Bits[10], in_2);
  and and_28 (and_28_out, Input_16_Bits[11], in_2);
  and and_29 (and_29_out, Input_16_Bits[12], in_2);
  and and_30 (and_30_out, Input_16_Bits[13], in_2);
  and and_31 (and_31_out, Input_16_Bits[14], in_2);
  and and_32 (and_32_out, Input_16_Bits[15], in_2);
  Clock clock_1 (.out(clock_1_out));
  S_R_Flip_Flop s_r_ff_1 (
    .S(and_17_out), .clk(clock_1_out), .R(and_1_out), .Q(Output_16_Bits[0]));  // open: Qn, preset, reset, en
  S_R_Flip_Flop s_r_ff_2 (
    .S(and_18_out), .clk(clock_1_out), .R(and_2_out), .Q(Output_16_Bits[1]));  // open: Qn, preset, reset, en
  S_R_Flip_Flop s_r_ff_3 (
    .S(and_19_out), .clk(clock_1_out), .R(and_3_out), .Q(Output_16_Bits[2]));  // open: Qn, preset, reset, en
  S_R_Flip_Flop s_r_ff_4 (
    .S(and_20_out), .clk(clock_1_out), .R(and_4_out), .Q(Output_16_Bits[3]));  // open: Qn, preset, reset, en
  S_R_Flip_Flop s_r_ff_5 (
    .S(and_21_out), .clk(clock_1_out), .R(and_5_out), .Q(Output_16_Bits[4]));  // open: Qn, preset, reset, en
  S_R_Flip_Flop s_r_ff_6 (
    .S(and_22_out), .clk(clock_1_out), .R(and_6_out), .Q(Output_16_Bits[5]));  // open: Qn, preset, reset, en
  S_R_Flip_Flop s_r_ff_7 (
    .S(and_23_out), .clk(clock_1_out), .R(and_7_out), .Q(Output_16_Bits[6]));  // open: Qn, preset, reset, en
  S_R_Flip_Flop s_r_ff_8 (
    .S(and_24_out), .clk(clock_1_out), .R(and_8_out), .Q(Output_16_Bits[7]));  // open: Qn, preset, reset, en
  S_R_Flip_Flop s_r_ff_9 (
    .S(and_25_out), .clk(clock_1_out), .R(and_9_out), .Q(Output_16_Bits[8]));  // open: Qn, preset, reset, en
  S_R_Flip_Flop s_r_ff_10 (
    .S(and_26_out), .clk(clock_1_out), .R(and_10_out), .Q(Output_16_Bits[9]));  // open: Qn, preset, reset, en
  S_R_Flip_Flop s_r_ff_11 (
    .S(and_27_out), .clk(clock_1_out), .R(and_11_out), .Q(Output_16_Bits[10]));  // open: Qn, preset, reset, en
  S_R_Flip_Flop s_r_ff_12 (
    .S(and_28_out), .clk(clock_1_out), .R(and_12_out), .Q(Output_16_Bits[11]));  // open: Qn, preset, reset, en
  S_R_Flip_Flop s_r_ff_13 (
    .S(and_29_out), .clk(clock_1_out), .R(and_13_out), .Q(Output_16_Bits[12]));  // open: Qn, preset, reset, en
  S_R_Flip_Flop s_r_ff_14 (
    .S(and_30_out), .clk(clock_1_out), .R(and_14_out), .Q(Output_16_Bits[13]));  // open: Qn, preset, reset, en
  S_R_Flip_Flop s_r_ff_15 (
    .S(and_31_out), .clk(clock_1_out), .R(and_15_out), .Q(Output_16_Bits[14]));  // open: Qn, preset, reset, en
  S_R_Flip_Flop s_r_ff_16 (
    .S(and_32_out), .clk(clock_1_out), .R(and_16_out), .Q(Output_16_Bits[15]));  // open: Qn, preset, reset, en
endmodule

module Register_Bank (
  input  [2:0] in_1,
  input  REGLOAD,
  input  [15:0] DATA_IN,
  output [15:0] DOUT1,
  output [15:0] DOUT2,
  output [15:0] DOUT3,
  output [15:0] DOUT4,
  output [15:0] DOUT5,
  output [15:0] DOUT6,
  output [15:0] DOUT7,
  output [15:0] DOUT8
);

  wire and_1_out, and_2_out, and_3_out, and_4_out, and_5_out, and_6_out, and_7_out, and_8_out,
       decoder_1_out0, decoder_1_out1, decoder_1_out2, decoder_1_out3, decoder_1_out4, decoder_1_out5,
       decoder_1_out6, decoder_1_out7;

  Decoder #(.select(3), .enable("false")) decoder_1 (
    .out0(decoder_1_out0), .out1(decoder_1_out1), .out2(decoder_1_out2), .out3(decoder_1_out3),
    .out4(decoder_1_out4), .out5(decoder_1_out5), .out6(decoder_1_out6), .out7(decoder_1_out7), .sel(in_1));
  and and_1 (and_1_out, decoder_1_out0, REGLOAD);
  and and_2 (and_2_out, decoder_1_out1, REGLOAD);
  and and_3 (and_3_out, decoder_1_out2, REGLOAD);
  and and_4 (and_4_out, decoder_1_out3, REGLOAD);
  and and_5 (and_5_out, decoder_1_out4, REGLOAD);
  and and_6 (and_6_out, decoder_1_out5, REGLOAD);
  and and_7 (and_7_out, decoder_1_out6, REGLOAD);
  and and_8 (and_8_out, decoder_1_out7, REGLOAD);
  _16_bit_register u_16_bit_register_1 (.Input_16_Bits(DATA_IN), .Output_16_Bits(DOUT1), .in_2(and_1_out));
  _16_bit_register u_16_bit_register_2 (.Input_16_Bits(DATA_IN), .Output_16_Bits(DOUT2), .in_2(and_2_out));
  _16_bit_register u_16_bit_register_3 (.Input_16_Bits(DATA_IN), .Output_16_Bits(DOUT3), .in_2(and_3_out));
  _16_bit_register u_16_bit_register_4 (.Input_16_Bits(DATA_IN), .Output_16_Bits(DOUT4), .in_2(and_4_out));
  _16_bit_register u_16_bit_register_5 (.Input_16_Bits(DATA_IN), .Output_16_Bits(DOUT5), .in_2(and_5_out));
  _16_bit_register u_16_bit_register_6 (.Input_16_Bits(DATA_IN), .Output_16_Bits(DOUT6), .in_2(and_6_out));
  _16_bit_register u_16_bit_register_7 (.Input_16_Bits(DATA_IN), .Output_16_Bits(DOUT7), .in_2(and_7_out));
  _16_bit_register u_16_bit_register_8 (.Input_16_Bits(DATA_IN), .Output_16_Bits(DOUT8), .in_2(and_8_out));
endmodule

module Control_unit (
  input  [3:0] OPCODE,
  input  ZF,
  output IRLD,
  output MEMLD,
  output MUX,
  output ZFLD,
  output REGLD,
  output ARMUX,
  output PCINC,
  output PCLD
);

  wire FETCH, not_1_out, not_2_out, not_3_out;
  wire [1:1] and_1_out;
  wire [3:0] _4_bit_register_output_4_bits, multiplexer_1_out, multiplexer_2_out;

  not not_1 (not_1_out, OPCODE[3]);
  not not_2 (not_2_out, OPCODE[1]);
  not not_3 (not_3_out, OPCODE[0]);
  and and_1 (and_1_out[1], not_1_out, OPCODE[2], not_2_out, not_3_out);
  Multiplexer #(.select(2), .width(4), .enable("false")) multiplexer_1 (
    .in0(OPCODE), .in1(OPCODE), .in2(4'b0000), .in3(4'b0101), .out(multiplexer_1_out),
    .sel({and_1_out[1], ZF}));
  Multiplexer #(.width(4), .enable("false")) multiplexer_2 (
    .in0(4'b0000), .in1(multiplexer_1_out), .out(multiplexer_2_out), .sel(FETCH));
  _4_bit_register _4_bit_register (
    .Input_4__Bits(multiplexer_2_out), .Output_4_Bits(_4_bit_register_output_4_bits));  // open: in_2
  ROM #(.addrWidth(4), .dataWidth(9)) rom_1 (
    .addr(_4_bit_register_output_4_bits), .data({FETCH, PCLD, PCINC, ARMUX, REGLD, ZFLD, MUX, MEMLD, IRLD}));  // open: sel
  // also tied to GND on the sheet: {multiplexer_1_out[0], multiplexer_1_out[1], multiplexer_1_out[2], multiplexer_1_out[3], _4_bit_register_output_4_bits[0], _4_bit_register_output_4_bits[1], _4_bit_register_output_4_bits[2], _4_bit_register_output_4_bits[3]}
endmodule

module _12_bit_register (
  input  [11:0] Input_16_Bits,
  input  in_2,
  output [11:0] Output_16_Bits
);

  wire and_1_out, and_2_out, and_3_out, and_4_out, and_5_out, and_6_out, and_7_out, and_8_out, and_9_out,
       and_10_out, and_11_out, and_12_out, and_13_out, and_14_out, and_15_out, and_16_out, and_17_out,
       and_18_out, and_19_out, and_20_out, and_21_out, and_22_out, and_23_out, and_24_out, clock_1_out,
       not_1_out, not_2_out, not_3_out, not_4_out, not_5_out, not_6_out, not_7_out, not_8_out, not_9_out,
       not_10_out, not_11_out, not_12_out;

  not not_1 (not_1_out, Input_16_Bits[0]);
  and and_1 (and_1_out, not_1_out, in_2);
  not not_2 (not_2_out, Input_16_Bits[1]);
  and and_2 (and_2_out, not_2_out, in_2);
  not not_3 (not_3_out, Input_16_Bits[2]);
  and and_3 (and_3_out, not_3_out, in_2);
  not not_4 (not_4_out, Input_16_Bits[3]);
  and and_4 (and_4_out, not_4_out, in_2);
  not not_5 (not_5_out, Input_16_Bits[4]);
  and and_5 (and_5_out, not_5_out, in_2);
  not not_6 (not_6_out, Input_16_Bits[5]);
  and and_6 (and_6_out, not_6_out, in_2);
  not not_7 (not_7_out, Input_16_Bits[6]);
  and and_7 (and_7_out, not_7_out, in_2);
  not not_8 (not_8_out, Input_16_Bits[7]);
  and and_8 (and_8_out, not_8_out, in_2);
  not not_9 (not_9_out, Input_16_Bits[8]);
  and and_9 (and_9_out, not_9_out, in_2);
  not not_10 (not_10_out, Input_16_Bits[9]);
  and and_10 (and_10_out, not_10_out, in_2);
  not not_11 (not_11_out, Input_16_Bits[10]);
  and and_11 (and_11_out, not_11_out, in_2);
  not not_12 (not_12_out, Input_16_Bits[11]);
  and and_12 (and_12_out, not_12_out, in_2);
  and and_13 (and_13_out, Input_16_Bits[0], in_2);
  and and_14 (and_14_out, Input_16_Bits[1], in_2);
  and and_15 (and_15_out, Input_16_Bits[2], in_2);
  and and_16 (and_16_out, Input_16_Bits[3], in_2);
  and and_17 (and_17_out, Input_16_Bits[4], in_2);
  and and_18 (and_18_out, Input_16_Bits[5], in_2);
  and and_19 (and_19_out, Input_16_Bits[6], in_2);
  and and_20 (and_20_out, Input_16_Bits[7], in_2);
  and and_21 (and_21_out, Input_16_Bits[8], in_2);
  and and_22 (and_22_out, Input_16_Bits[9], in_2);
  and and_23 (and_23_out, Input_16_Bits[10], in_2);
  and and_24 (and_24_out, Input_16_Bits[11], in_2);
  Clock clock_1 (.out(clock_1_out));
  S_R_Flip_Flop s_r_ff_1 (
    .S(and_13_out), .clk(clock_1_out), .R(and_1_out), .Q(Output_16_Bits[0]));  // open: Qn, preset, reset, en
  S_R_Flip_Flop s_r_ff_2 (
    .S(and_14_out), .clk(clock_1_out), .R(and_2_out), .Q(Output_16_Bits[1]));  // open: Qn, preset, reset, en
  S_R_Flip_Flop s_r_ff_3 (
    .S(and_15_out), .clk(clock_1_out), .R(and_3_out), .Q(Output_16_Bits[2]));  // open: Qn, preset, reset, en
  S_R_Flip_Flop s_r_ff_4 (
    .S(and_16_out), .clk(clock_1_out), .R(and_4_out), .Q(Output_16_Bits[3]));  // open: Qn, preset, reset, en
  S_R_Flip_Flop s_r_ff_5 (
    .S(and_17_out), .clk(clock_1_out), .R(and_5_out), .Q(Output_16_Bits[4]));  // open: Qn, preset, reset, en
  S_R_Flip_Flop s_r_ff_6 (
    .S(and_18_out), .clk(clock_1_out), .R(and_6_out), .Q(Output_16_Bits[5]));  // open: Qn, preset, reset, en
  S_R_Flip_Flop s_r_ff_7 (
    .S(and_19_out), .clk(clock_1_out), .R(and_7_out), .Q(Output_16_Bits[6]));  // open: Qn, preset, reset, en
  S_R_Flip_Flop s_r_ff_8 (
    .S(and_20_out), .clk(clock_1_out), .R(and_8_out), .Q(Output_16_Bits[7]));  // open: Qn, preset, reset, en
  S_R_Flip_Flop s_r_ff_9 (
    .S(and_21_out), .clk(clock_1_out), .R(and_9_out), .Q(Output_16_Bits[8]));  // open: Qn, preset, reset, en
  S_R_Flip_Flop s_r_ff_10 (
    .S(and_22_out), .clk(clock_1_out), .R(and_10_out), .Q(Output_16_Bits[9]));  // open: Qn, preset, reset, en
  S_R_Flip_Flop s_r_ff_11 (
    .S(and_23_out), .clk(clock_1_out), .R(and_11_out), .Q(Output_16_Bits[10]));  // open: Qn, preset, reset, en
  S_R_Flip_Flop s_r_ff_12 (
    .S(and_24_out), .clk(clock_1_out), .R(and_12_out), .Q(Output_16_Bits[11]));  // open: Qn, preset, reset, en
endmodule

module _4_bit_register (
  input  [3:0] Input_4__Bits,
  input  in_2,
  output [3:0] Output_4_Bits
);

  wire and_1_out, and_2_out, and_3_out, and_4_out, and_5_out, and_6_out, and_7_out, and_8_out, clock_1_out,
       not_1_out, not_2_out, not_3_out, not_4_out;

  and and_1 (and_1_out, Input_4__Bits[0], in_2);
  not not_1 (not_1_out, Input_4__Bits[0]);
  and and_2 (and_2_out, not_1_out, in_2);
  and and_3 (and_3_out, Input_4__Bits[1], in_2);
  not not_2 (not_2_out, Input_4__Bits[1]);
  and and_4 (and_4_out, not_2_out, in_2);
  and and_5 (and_5_out, Input_4__Bits[2], in_2);
  not not_3 (not_3_out, Input_4__Bits[2]);
  and and_6 (and_6_out, not_3_out, in_2);
  and and_7 (and_7_out, Input_4__Bits[3], in_2);
  not not_4 (not_4_out, Input_4__Bits[3]);
  and and_8 (and_8_out, not_4_out, in_2);
  Clock clock_1 (.out(clock_1_out));
  S_R_Flip_Flop s_r_ff_1 (
    .S(and_1_out), .clk(clock_1_out), .R(and_2_out), .Q(Output_4_Bits[0]));  // open: Qn, preset, reset, en
  S_R_Flip_Flop s_r_ff_2 (
    .S(and_3_out), .clk(clock_1_out), .R(and_4_out), .Q(Output_4_Bits[1]));  // open: Qn, preset, reset, en
  S_R_Flip_Flop s_r_ff_3 (
    .S(and_5_out), .clk(clock_1_out), .R(and_6_out), .Q(Output_4_Bits[2]));  // open: Qn, preset, reset, en
  S_R_Flip_Flop s_r_ff_4 (
    .S(and_7_out), .clk(clock_1_out), .R(and_8_out), .Q(Output_4_Bits[3]));  // open: Qn, preset, reset, en
endmodule

module _1_bit_register (
  input  Input_16_Bits,
  input  in_2,
  output Output_16_Bits
);

  wire and_1_out, and_2_out, clock_1_out, not_1_out;

  and and_1 (and_1_out, Input_16_Bits, in_2);
  not not_1 (not_1_out, Input_16_Bits);
  and and_2 (and_2_out, not_1_out, in_2);
  Clock clock_1 (.out(clock_1_out));
  S_R_Flip_Flop s_r_ff_1 (
    .S(and_1_out), .clk(clock_1_out), .R(and_2_out), .Q(Output_16_Bits));  // open: Qn, preset, reset, en
endmodule

module PC (
  input  [11:0] ADDR_IN,
  input  PCinc,
  input  PCld,
  output [11:0] ADDR_OUT
);

  wire or_1_out;
  wire [11:0] adder_1_out, multiplexer_1_out;

  Adder #(.width(12)) adder_1 (.a(12'h1), .b(ADDR_OUT), .out(adder_1_out));  // open: cin, cout
  Multiplexer #(.width(12), .enable("false")) multiplexer_1 (
    .in0(ADDR_IN), .in1(adder_1_out), .out(multiplexer_1_out), .sel(PCinc));
  or or_1 (or_1_out, PCinc, PCld);
  // _12_bit_register _12_bit_register: pin names not known; wires that end beside it: multiplexer_1_out, or_1_out, ADDR_OUT
endmodule

module CPU (
  input  [15:0] Register_0,
  input  [15:0] D_IN,
  input  [15:0] D_OUT,
  input  [11:0] ADDR
);

  wire ALU_zf, ARMUX, IRLD, MEMLD, MUX, PCINC, PCLD, REGLD, ZF, ZFLD;
  wire [11:0] adder_1_out, DATA_ADDR, INST_ADDR, IR;
  wire [15:0] D_in_t, multiplexer_1_out, R3, Register_Bank_dout2, Register_Bank_dout3, Register_Bank_dout4,
       Register_Bank_dout5, Register_Bank_dout6, Register_Bank_dout7, Register_Bank_dout8;
  wire [15:12] R2;

  Clock clock_1 ();  // open: out
  Adder #(.width(12)) adder_1 (.a(INST_ADDR), .b(IR), .out(adder_1_out));  // open: cin, cout
  ALU ALU (.R3(R3), .A(D_OUT), .B({R2, DATA_ADDR}), .ZF(ALU_zf), .IR_11_9(IR[11:9]), .IR_8_6(IR[8:6]));
  _1_bit_register u_1_bit_register_1 (.Input_16_Bits(ALU_zf), .in_2(ZFLD), .Output_16_Bits(ZF));
  Multiplexer #(.width(16), .enable("false")) multiplexer_1 (.in0(R3), .in1(D_IN), .out(multiplexer_1_out), .sel(MUX));
  PC PC (.ADDR_IN(adder_1_out), .ADDR_OUT(INST_ADDR), .PCinc(PCINC), .PCld(PCLD));
  Register_Bank Register_Bank (
    .in_1(IR[2:0]), .REGLOAD(REGLD), .DATA_IN(multiplexer_1_out), .DOUT1(Register_0),
    .DOUT2(Register_Bank_dout2), .DOUT3(Register_Bank_dout3), .DOUT4(Register_Bank_dout4),
    .DOUT5(Register_Bank_dout5), .DOUT6(Register_Bank_dout6), .DOUT7(Register_Bank_dout7),
    .DOUT8(Register_Bank_dout8));
  Multiplexer #(.select(3), .width(16), .enable("false")) multiplexer_2 (
    .in0(Register_0), .in1(Register_Bank_dout2), .in2(Register_Bank_dout3), .in3(Register_Bank_dout4),
    .in4(Register_Bank_dout5), .in5(Register_Bank_dout6), .in6(Register_Bank_dout7),
    .in7(Register_Bank_dout8), .out(D_OUT), .sel(IR[8:6]));
  Control_unit Control_Unit (
    .OPCODE({D_in_t[12], D_in_t[13], D_in_t[14], D_in_t[15]}), .ZF(ZF), .IRLD(IRLD), .MEMLD(MEMLD),
    .MUX(MUX), .ZFLD(ZFLD), .REGLD(REGLD), .ARMUX(ARMUX), .PCINC(PCINC), .PCLD(PCLD));
  Multiplexer #(.select(3), .width(16), .enable("false")) multiplexer_3 (
    .in0(Register_0), .in1(Register_Bank_dout2), .in2(Register_Bank_dout3), .in3(Register_Bank_dout4),
    .in4(Register_Bank_dout5), .in5(Register_Bank_dout6), .in6(Register_Bank_dout7),
    .in7(Register_Bank_dout8), .out({R2, DATA_ADDR}), .sel(IR[5:3]));
  Multiplexer #(.width(12), .enable("false")) multiplexer_4 (.in0(INST_ADDR), .in1(DATA_ADDR), .out(ADDR), .sel(ARMUX));
  _12_bit_register _12_bit_register (.Input_16_Bits(D_in_t[11:0]), .in_2(IRLD), .Output_16_Bits(IR));
  // also tied to GND on the sheet: {DATA_ADDR[0], DATA_ADDR[1], DATA_ADDR[2], DATA_ADDR[3], DATA_ADDR[4], DATA_ADDR[5], DATA_ADDR[6], DATA_ADDR[7], DATA_ADDR[8], DATA_ADDR[9], DATA_ADDR[10], DATA_ADDR[11], D_OUT[0], D_OUT[1], D_OUT[2], D_OUT[3], D_OUT[4], D_OUT[5], D_OUT[6], D_OUT[7], D_OUT[8], D_OUT[9], D_OUT[10], D_OUT[11], D_OUT[12], D_OUT[13], D_OUT[14], D_OUT[15], R2[12], R2[13], R2[14], R2[15]}

  // Other names for the same wires on the sheet: R2[11:0] = DATA_ADDR; IR_2_0[2:0] = IR[2:0]; IR_5_3[2:0] = IR[5:3];
  //   IR_8_6[2:0] = IR[8:6]; IR_11_9[2:0] = IR[11:9]; OPCODE[3:0] = {D_in_t[12], D_in_t[13], D_in_t[14], D_in_t[15]};
  //   R1[15:0] = D_OUT
endmodule
